# Fritzing sketch Circuit Diagram (saved by Fritzing 0.9.3b)
breadboards: 2

parts:
  Composant1 = Adafruit ADS1115 16Bit I2C ADC [part_number="Adafruit #1085"]
  R1 = Rotary Potentiometer (Small) [maximum_resistance=100kΩ package=THT]
  R2 = Rotary Potentiometer (Small) [maximum_resistance=100kΩ package=THT]
  R3 = Rotary Potentiometer (Small) [maximum_resistance=100kΩ package=THT]
  U2 = NodeMCU V1.0
  U4 = NodeMCU V1.0
  J5 = Basic Servo
  J6 = Basic Servo
  J7 = Basic Servo

nets:
  N1: Composant1.AIN2, R3.wiper
  N2: Composant1.AIN1, R2.wiper
  N3: Composant1.AIN0, R1.wiper
  N4: Composant1.SDA, U2.D2
  N5: Composant1.SCL, U2.D1
  GND: Composant1.GND, R1.leg2, R2.leg2, R3.leg2, U2.GND
  VDD: Composant1.VDD, R1.leg1, R2.leg1, R3.leg1, U2.3V3
  GND_2: U4.GND, J5.gnd, J6.gnd, J7.gnd
  N6: U4.D5, J7.pulse
  VCC: U4.D6, J5.vcc, J6.vcc, J6.pulse, J7.vcc
  N7: U4.D7, J5.pulse

custom parts:
  Adafruit ADS1115 16Bit I2C ADC: For microcontrollers without an analog-to-digital converter or when you want a higher-precision ADC, the ADS1115 provides 16-bit precision at 860 samples/second over I2C. The chip can be configured as 4 single-ended input channels, or two differential channels. As a nice bonus, it even includes a programmable gain amplifier, up to x16, to help boost up smaller single/differential signals to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
  NodeMCU V1.0: ESP8266 based NodeMCU
